# Fritzing sketch WellDepthTemperature (saved by Fritzing 0.9.3b)
breadboards: 1

parts:
  Part1 = SparkFun ESP8266 Thing
  D1 = Rectifier Diode [part_number=1N4001 package="300 mil [THT]"]
  D2 = Rectifier Diode [part_number=1N4001 package="300 mil [THT]"]
  R1 = Resistor [tolerance=±5% resistance=4.7k package="0402 [SMD]"]
  J1 = female pin header, 8 pins [form="♀ (female)"]

nets:
  N1: Part1.GND, D1.anode, J1.pin2, J1.pin4
  N2: Part1.VCC, D2.cathode, R1.Pin_1, J1.pin3
  N3: Part1.GPIO4, D1.cathode, D2.anode, R1.Pin_0, J1.pin1

notes:
  To Do: Decide which 4 RJ45 pins to connect to.
  The diodes protect against over- and under-voltage on the 1-wire bus.
  The resistor is a pull-up resistor for the 1-wire bus.
  "connector" is the Sparkfun RJ45 Breakout board.
